# Fritzing sketch rampart (saved by Fritzing 0.9.3b)
breadboards: 1

parts:
  Part1 = Arduino Nano (Rev3.0)
  R1 = Rotary Potentiometer (Small) [maximum_resistance=100kΩ package=THT]  # not connected
  J1 = Piezo Speaker

nets:
  N1: Part1.D9, J1.pin2
